# Fritzing sketch ble_dimmer (saved by Fritzing 0.9.3b)
perfboards: 2

parts:
  Part1 = Arduino Pro Mini v13
  U1 = Optocoupler [package=THT]
  D1 = Rectifier Diode [package="Melf DO-213 AA [SMD]"]
  D2 = Rectifier Diode [package="Melf DO-213 AA [SMD]"]
  D3 = Rectifier Diode [package="Melf DO-213 AA [SMD]"]
  D4 = Rectifier Diode [package="Melf DO-213 AA [SMD]"]
  R1 = Resistor [tolerance=±5% resistance=66k package="2512 [SMD]"]
  R2 = Resistor [tolerance=±5% resistance=66k package="2512 [SMD]"]
  R3 = Resistor [tolerance=±5% resistance=10k package="0805 [SMD]"]
  R4 = Resistor [tolerance=±5% resistance=220 package="0805 [SMD]"]
  U3 = MOC3031-M [package=dil06]
  R5 = Resistor [tolerance=±5% resistance=1k package="0805 [SMD]"]
  R7 = Resistor [tolerance=±5% resistance=1k package="0805 [SMD]"]
  R6 = Resistor [tolerance=±5% resistance=220 package="0805 [SMD]"]
  U5 = MOC3031-M [package=dil06]
  J3 = Screw terminal - 2 pins [part_number="AC 220V" package=THT]
  HLK-PM1 = HLK-PM01
  J2 = Screw terminal - 2 pins [package=THT]
  TRI1 = BTA Triac [package="TO220 [THT]"]
  TRI2 = BTA Triac [package="TO220 [THT]"]
  J5 = female pin header, 3 pins [form="♀ (female)"]
  J6 = female pin header, 3 pins [form="♀ (female)"]
  J8 = female pin header, 3 pins [form="♀ (female)"]
  J7 = female pin header, 3 pins [form="♀ (female)"]
  LED3 = LED - 5mm [color="Yellow (592nm)" package="5 mm [THT]"]
  LED4 = LED - 5mm [color="Yellow (592nm)" package="5 mm [THT]"]
  Part4 = Bluetooth HC-05 Macho
  R8 = Resistor [tolerance=±5% resistance=66k package="2512 [SMD]"]
  R9 = Resistor [tolerance=±5% resistance=66k package="2512 [SMD]"]

nets:
  5V: Part1.VCC, R3.Pin_1, J6.pin1, J7.pin1, Part4.VCC
  GND: Part1.GND, U1.Pin_4, U3.2, U5.2, HLK-PM1.-Vo, J5.pin1, J8.pin1, Part4.GND
  N1: Part1.RAW, J8.pin3
  N2: Part1.D11_PWM/MOSI, Part4.RXD
  N3: Part1.D10_PWM/SS, Part4.TXD
  N4: Part1.D5_PWM, R6.Pin_0
  N5: Part1.D3_PWM, R4.Pin_0
  N6: Part1.D2, J8.pin2
  N7: U1.Pin_1, D2.cathode, D4.cathode
  N8: U1.Pin_2, D1.anode, D3.anode
  N9: U1.Pin_5, R3.Pin_0, J5.pin2
  N10: D1.cathode, D2.anode, R1.Pin_1, R8.Pin_1
  N11: D3.cathode, D4.anode, R2.Pin_1, R9.Pin_1
  N12: R1.Pin_0, R5.Pin_1, R7.Pin_1, J3.pin1, HLK-PM1.AC#1, TRI1.A2, TRI2.A2, R8.Pin_0
  N13: R2.Pin_0, J3.pin2, HLK-PM1.AC#0, R9.Pin_0
  N14: R4.Pin_1, LED3.anode
  N15: U3.1, J6.pin2
  N16: U3.4, TRI1.G
  N17: U3.6, R5.Pin_0
  N18: R7.Pin_0, U5.6
  N19: R6.Pin_1, LED4.anode
  N20: U5.1, J6.pin3
  N21: U5.4, TRI2.G
  N22: HLK-PM1.+Vo, J5.pin3
  N23: J2.pin1, TRI2.A1
  N24: J2.pin2, TRI1.A1
  N25: J7.pin2, LED4.cathode
  N26: J7.pin3, LED3.cathode

custom parts:
  BTA Triac: BTA16
